// Logisim project CPU_MIPS_unidad_control_v2017_05.circ as structural Verilog: 10 circuits, main circuit Main
module BANCO (
  input  [4:0] RA,
  input  [4:0] RB,
  input  [4:0] RC,
  input  [31:0] C_IN,
  input  Load_EN,
  input  CLOCK_IN,
  input  RESET_IN,
  output [31:0] A_OUT,
  output [31:0] B_OUT
);

  wire [3:0] demultiplexer_2_out0, demultiplexer_2_out4, demultiplexer_2_out8, demultiplexer_2_out12,
       demultiplexer_2_out16, demultiplexer_2_out20, demultiplexer_2_out24, demultiplexer_2_out28;
  wire [31:0] demultiplexer_1_out0, demultiplexer_1_out1, demultiplexer_1_out2, demultiplexer_1_out3,
       demultiplexer_1_out4, demultiplexer_1_out5, demultiplexer_1_out6, demultiplexer_1_out7,
       demultiplexer_1_out8, demultiplexer_1_out9, demultiplexer_1_out10, demultiplexer_1_out11,
       demultiplexer_1_out12, demultiplexer_1_out13, demultiplexer_1_out14, demultiplexer_1_out15,
       demultiplexer_1_out16, demultiplexer_1_out17, demultiplexer_1_out18, demultiplexer_1_out19,
       demultiplexer_1_out20, demultiplexer_1_out21, demultiplexer_1_out22, demultiplexer_1_out23,
       demultiplexer_1_out24, demultiplexer_1_out25, demultiplexer_1_out26, demultiplexer_1_out27,
       demultiplexer_1_out28, demultiplexer_1_out29, demultiplexer_1_out30, demultiplexer_1_out31,
       register_1_q, register_2_q, register_3_q, register_4_q, register_5_q, register_6_q, register_7_q,
       register_8_q, register_9_q, register_10_q, register_11_q, register_12_q, register_13_q, register_14_q,
       register_15_q, register_16_q, register_17_q, register_18_q, register_19_q, register_20_q,
       register_21_q, register_22_q, register_23_q, register_24_q, register_25_q, register_26_q,
       register_27_q, register_28_q, register_29_q, register_30_q, register_31_q, register_32_q;

  Register #(.width(32)) register_1 (
    .D(demultiplexer_1_out0), .en(1'b0), .Q(register_1_q), .clk(CLOCK_IN), .clr(RESET_IN));
  Register #(.width(32)) register_2 (
    .D(demultiplexer_1_out1), .en(demultiplexer_2_out0[1]), .Q(register_2_q), .clk(CLOCK_IN), .clr(RESET_IN));
  Register #(.width(32)) register_3 (
    .D(demultiplexer_1_out2), .en(demultiplexer_2_out0[2]), .Q(register_3_q), .clk(CLOCK_IN), .clr(RESET_IN));
  Register #(.width(32)) register_4 (
    .D(demultiplexer_1_out3), .en(demultiplexer_2_out0[3]), .Q(register_4_q), .clk(CLOCK_IN), .clr(RESET_IN));
  Demultiplexer #(.select(5), .width(32)) demultiplexer_1 (
    .out0(demultiplexer_1_out0), .out1(demultiplexer_1_out1), .out2(demultiplexer_1_out2),
    .out3(demultiplexer_1_out3), .out4(demultiplexer_1_out4), .out5(demultiplexer_1_out5),
    .out6(demultiplexer_1_out6), .out7(demultiplexer_1_out7), .out8(demultiplexer_1_out8),
    .out9(demultiplexer_1_out9), .out10(demultiplexer_1_out10), .out11(demultiplexer_1_out11),
    .out12(demultiplexer_1_out12), .out13(demultiplexer_1_out13), .out14(demultiplexer_1_out14),
    .out15(demultiplexer_1_out15), .out16(demultiplexer_1_out16), .out17(demultiplexer_1_out17),
    .out18(demultiplexer_1_out18), .out19(demultiplexer_1_out19), .out20(demultiplexer_1_out20),
    .out21(demultiplexer_1_out21), .out22(demultiplexer_1_out22), .out23(demultiplexer_1_out23),
    .out24(demultiplexer_1_out24), .out25(demultiplexer_1_out25), .out26(demultiplexer_1_out26),
    .out27(demultiplexer_1_out27), .out28(demultiplexer_1_out28), .out29(demultiplexer_1_out29),
    .out30(demultiplexer_1_out30), .out31(demultiplexer_1_out31), .in(C_IN), .sel(RC));  // open: en
  Register #(.width(32)) register_5 (
    .D(demultiplexer_1_out4), .en(demultiplexer_2_out4[0]), .Q(register_5_q), .clk(CLOCK_IN), .clr(RESET_IN));
  Register #(.width(32)) register_6 (
    .D(demultiplexer_1_out5), .en(demultiplexer_2_out4[1]), .Q(register_6_q), .clk(CLOCK_IN), .clr(RESET_IN));
  Register #(.width(32)) register_7 (
    .D(demultiplexer_1_out6), .en(demultiplexer_2_out4[2]), .Q(register_7_q), .clk(CLOCK_IN), .clr(RESET_IN));
  Register #(.width(32)) register_8 (
    .D(demultiplexer_1_out7), .en(demultiplexer_2_out4[3]), .Q(register_8_q), .clk(CLOCK_IN), .clr(RESET_IN));
  Register #(.width(32)) register_9 (
    .D(demultiplexer_1_out8), .en(demultiplexer_2_out8[0]), .Q(register_9_q), .clk(CLOCK_IN), .clr(RESET_IN));
  Register #(.width(32)) register_10 (
    .D(demultiplexer_1_out9), .en(demultiplexer_2_out8[1]), .Q(register_10_q), .clk(CLOCK_IN), .clr(RESET_IN));
  Register #(.width(32)) register_11 (
    .D(demultiplexer_1_out10), .en(demultiplexer_2_out8[2]), .Q(register_11_q), .clk(CLOCK_IN), .clr(RESET_IN));
  Register #(.width(32)) register_12 (
    .D(demultiplexer_1_out11), .en(demultiplexer_2_out8[3]), .Q(register_12_q), .clk(CLOCK_IN), .clr(RESET_IN));
  Register #(.width(32)) register_13 (
    .D(demultiplexer_1_out12), .en(demultiplexer_2_out12[0]), .Q(register_13_q), .clk(CLOCK_IN),
    .clr(RESET_IN));
  Register #(.width(32)) register_14 (
    .D(demultiplexer_1_out13), .en(demultiplexer_2_out12[1]), .Q(register_14_q), .clk(CLOCK_IN),
    .clr(RESET_IN));
  Register #(.width(32)) register_15 (
    .D(demultiplexer_1_out14), .en(demultiplexer_2_out12[2]), .Q(register_15_q), .clk(CLOCK_IN),
    .clr(RESET_IN));
  Register #(.width(32)) register_16 (
    .D(demultiplexer_1_out15), .en(demultiplexer_2_out12[3]), .Q(register_16_q), .clk(CLOCK_IN),
    .clr(RESET_IN));
  Register #(.width(32)) register_17 (
    .D(demultiplexer_1_out16), .en(demultiplexer_2_out16[0]), .Q(register_17_q), .clk(CLOCK_IN),
    .clr(RESET_IN));
  Register #(.width(32)) register_18 (
    .D(demultiplexer_1_out17), .en(demultiplexer_2_out16[1]), .Q(register_18_q), .clk(CLOCK_IN),
    .clr(RESET_IN));
  Register #(.width(32)) register_19 (
    .D(demultiplexer_1_out18), .en(demultiplexer_2_out16[2]), .Q(register_19_q), .clk(CLOCK_IN),
    .clr(RESET_IN));
  Register #(.width(32)) register_20 (
    .D(demultiplexer_1_out19), .en(demultiplexer_2_out16[3]), .Q(register_20_q), .clk(CLOCK_IN),
    .clr(RESET_IN));
  Register #(.width(32)) register_21 (
    .D(demultiplexer_1_out20), .en(demultiplexer_2_out20[0]), .Q(register_21_q), .clk(CLOCK_IN),
    .clr(RESET_IN));
  Register #(.width(32)) register_22 (
    .D(demultiplexer_1_out21), .en(demultiplexer_2_out20[1]), .Q(register_22_q), .clk(CLOCK_IN),
    .clr(RESET_IN));
  Register #(.width(32)) register_23 (
    .D(demultiplexer_1_out22), .en(demultiplexer_2_out20[2]), .Q(register_23_q), .clk(CLOCK_IN),
    .clr(RESET_IN));
  Register #(.width(32)) register_24 (
    .D(demultiplexer_1_out23), .en(demultiplexer_2_out20[3]), .Q(register_24_q), .clk(CLOCK_IN),
    .clr(RESET_IN));
  Register #(.width(32)) register_25 (
    .D(demultiplexer_1_out24), .en(demultiplexer_2_out24[0]), .Q(register_25_q), .clk(CLOCK_IN),
    .clr(RESET_IN));
  Register #(.width(32)) register_26 (
    .D(demultiplexer_1_out25), .en(demultiplexer_2_out24[1]), .Q(register_26_q), .clk(CLOCK_IN),
    .clr(RESET_IN));
  Register #(.width(32)) register_27 (
    .D(demultiplexer_1_out26), .en(demultiplexer_2_out24[2]), .Q(register_27_q), .clk(CLOCK_IN),
    .clr(RESET_IN));
  Register #(.width(32)) register_28 (
    .D(demultiplexer_1_out27), .en(demultiplexer_2_out24[3]), .Q(register_28_q), .clk(CLOCK_IN),
    .clr(RESET_IN));
  Register #(.width(32)) register_29 (
    .D(demultiplexer_1_out28), .en(demultiplexer_2_out28[0]), .Q(register_29_q), .clk(CLOCK_IN),
    .clr(RESET_IN));
  Register #(.width(32)) register_30 (
    .D(demultiplexer_1_out29), .en(demultiplexer_2_out28[1]), .Q(register_30_q), .clk(CLOCK_IN),
    .clr(RESET_IN));
  Register #(.width(32)) register_31 (
    .D(demultiplexer_1_out30), .en(demultiplexer_2_out28[2]), .Q(register_31_q), .clk(CLOCK_IN),
    .clr(RESET_IN));
  Register #(.width(32)) register_32 (
    .D(demultiplexer_1_out31), .en(demultiplexer_2_out28[3]), .Q(register_32_q), .clk(CLOCK_IN),
    .clr(RESET_IN));
  Demultiplexer #(.select(5), .enable("false")) demultiplexer_2 (
    .out0(demultiplexer_2_out0[0]), .out1(demultiplexer_2_out0[1]), .out2(demultiplexer_2_out0[2]),
    .out3(demultiplexer_2_out0[3]), .out4(demultiplexer_2_out4[0]), .out5(demultiplexer_2_out4[1]),
    .out6(demultiplexer_2_out4[2]), .out7(demultiplexer_2_out4[3]), .out8(demultiplexer_2_out8[0]),
    .out9(demultiplexer_2_out8[1]), .out10(demultiplexer_2_out8[2]), .out11(demultiplexer_2_out8[3]),
    .out12(demultiplexer_2_out12[0]), .out13(demultiplexer_2_out12[1]), .out14(demultiplexer_2_out12[2]),
    .out15(demultiplexer_2_out12[3]), .out16(demultiplexer_2_out16[0]), .out17(demultiplexer_2_out16[1]),
    .out18(demultiplexer_2_out16[2]), .out19(demultiplexer_2_out16[3]), .out20(demultiplexer_2_out20[0]),
    .out21(demultiplexer_2_out20[1]), .out22(demultiplexer_2_out20[2]), .out23(demultiplexer_2_out20[3]),
    .out24(demultiplexer_2_out24[0]), .out25(demultiplexer_2_out24[1]), .out26(demultiplexer_2_out24[2]),
    .out27(demultiplexer_2_out24[3]), .out28(demultiplexer_2_out28[0]), .out29(demultiplexer_2_out28[1]),
    .out30(demultiplexer_2_out28[2]), .out31(demultiplexer_2_out28[3]), .in(Load_EN), .sel(RC));
  Multiplexer #(.select(5), .width(32), .enable("false")) multiplexer_1 (
    .in0(register_1_q), .in1(register_2_q), .in2(register_3_q), .in3(register_4_q), .in4(register_5_q),
    .in5(register_6_q), .in6(register_7_q), .in7(register_8_q), .in8(register_9_q), .in9(register_10_q),
    .in10(register_11_q), .in11(register_12_q), .in12(register_13_q), .in13(register_14_q),
    .in14(register_15_q), .in15(register_16_q), .in16(register_17_q), .in17(register_18_q),
    .in18(register_19_q), .in19(register_20_q), .in20(register_21_q), .in21(register_22_q),
    .in22(register_23_q), .in23(register_24_q), .in24(register_25_q), .in25(register_26_q),
    .in26(register_27_q), .in27(register_28_q), .in28(register_29_q), .in29(register_30_q),
    .in30(register_31_q), .in31(register_32_q), .out(A_OUT), .sel(RA));
  Multiplexer #(.select(5), .width(32), .disabled(0), .enable("false")) multiplexer_2 (
    .in0(register_1_q), .in1(register_2_q), .in2(register_3_q), .in3(register_4_q), .in4(register_5_q),
    .in5(register_6_q), .in6(register_7_q), .in7(register_8_q), .in8(register_9_q), .in9(register_10_q),
    .in10(register_11_q), .in11(register_12_q), .in12(register_13_q), .in13(register_14_q),
    .in14(register_15_q), .in15(register_16_q), .in16(register_17_q), .in17(register_18_q),
    .in18(register_19_q), .in19(register_20_q), .in20(register_21_q), .in21(register_22_q),
    .in22(register_23_q), .in23(register_24_q), .in24(register_25_q), .in25(register_26_q),
    .in26(register_27_q), .in27(register_28_q), .in28(register_29_q), .in29(register_30_q),
    .in30(register_31_q), .in31(register_32_q), .out(B_OUT), .sel(RB));

  // Other names for the same wires on the sheet: CLK = CLOCK_IN; RST = RESET_IN
endmodule

// MAIN
module Main (
  input  RESET,
  output [31:0] BUS_DE_DATOS,
  output [31:0] BUS_INTERNO,
  output [31:0] INDICADORES,
  output [31:0] SALIDA_ALU
);

  wire C1, C2, C3, C4, C5, C6, C7, C8, C9, C10, C11, CLK, E, ENABLE_B, L, M_Sel, MA, MB, or_1_out, or_2_out,
       or_3_out, T1, T2, T3, T4, T5, T6, T7, T8, T9, TA;
  wire [1:0] MAR_q_2;
  wire [4:0] RA, RB, RC;
  wire [5:0] func;
  wire [31:0] adder_1_out, banco_1_a_out, banco_1_b_out, bit_extender_1_out, IND_q, MAR_q, MBR_q,
       multiplexer_1_out, multiplexer_2_out, multiplexer_3_out, multiplexer_4_out, multiplexer_5_out, PC_q,
       RI, RT1_q, RT2_q, RT3_q;

  Register #(.width(32)) MAR (
    .D(BUS_INTERNO), .en(C1), .Q({MAR_q[31:14], MAR_q_2, MAR_q[11:0]}), .clk(CLK), .clr(RESET));
  assign BUS_INTERNO = T1 ? banco_1_a_out : 32'bz;  // Controlled_Buffer controlled_buffer_1
  assign BUS_INTERNO = T2 ? banco_1_b_out : 32'bz;  // Controlled_Buffer controlled_buffer_2
  BANCO banco_1 (
    .RA(RA), .RB(RB), .RC(RC), .C_IN(BUS_INTERNO), .Load_EN(ENABLE_B), .CLOCK_IN(CLK), .RESET_IN(RESET),
    .A_OUT(banco_1_a_out), .B_OUT(banco_1_b_out));
  Register #(.width(32)) RT1 (.D(BUS_INTERNO), .en(C9), .Q(RT1_q), .clk(CLK), .clr(RESET));
  Multiplexer #(.width(32), .enable("false")) multiplexer_1 (
    .in0(banco_1_a_out), .in1(RT1_q), .out(multiplexer_1_out), .sel(MA));
  ALU alu_1 (.Op__A(multiplexer_1_out), .Op__B(multiplexer_3_out), .C_OP(func), .Estado(INDICADORES), .S(SALIDA_ALU));
  RAM #(.addrWidth(24), .dataWidth(32)) ram_1 (
    .addr({MAR_q[25:14], MAR_q_2, MAR_q[11:2]}), .data(BUS_DE_DATOS), .sel(E), .clk(CLK), .ld(L));  // open: clr
  Multiplexer #(.width(32), .enable("false")) multiplexer_2 (
    .in0(BUS_DE_DATOS), .in1(BUS_INTERNO), .out(multiplexer_2_out), .sel(C3));
  or or_1 (or_1_out, C2, C3);
  assign BUS_DE_DATOS = TA ? MBR_q : 32'bz;  // Controlled_Buffer controlled_buffer_3
  Register #(.width(32)) MBR (.D(multiplexer_2_out), .en(or_1_out), .Q(MBR_q), .clk(CLK), .clr(RESET));
  assign BUS_INTERNO = T3 ? MBR_q : 32'bz;  // Controlled_Buffer controlled_buffer_4
  assign BUS_INTERNO = T5 ? SALIDA_ALU : 32'bz;  // Controlled_Buffer controlled_buffer_5
  Register #(.width(32)) RT2 (.D(BUS_INTERNO), .en(C10), .Q(RT2_q), .clk(CLK), .clr(RESET));
  Multiplexer #(.width(32), .enable("false")) multiplexer_3 (
    .in0(banco_1_b_out), .in1(RT2_q), .out(multiplexer_3_out), .sel(MB));
  assign BUS_INTERNO = T6 ? RT3_q : 32'bz;  // Controlled_Buffer controlled_buffer_6
  Register #(.width(32)) RT3 (.D(SALIDA_ALU), .en(C11), .Q(RT3_q), .clk(CLK), .clr(RESET));
  Adder #(.width(32)) adder_1 (.a(PC_q), .b(32'h4), .out(adder_1_out));  // open: cin, cout
  Register #(.width(32)) PC (.D(multiplexer_4_out), .en(or_2_out), .Q(PC_q), .clk(CLK), .clr(RESET));
  Multiplexer #(.width(32), .enable("false")) multiplexer_4 (
    .in0(adder_1_out), .in1(BUS_INTERNO), .out(multiplexer_4_out), .sel(C5));
  or or_2 (or_2_out, C4, C5);
  assign BUS_INTERNO = T4 ? PC_q : 32'bz;  // Controlled_Buffer controlled_buffer_7
  Multiplexer #(.width(32), .enable("false")) multiplexer_5 (
    .in0(BUS_INTERNO), .in1(INDICADORES), .out(multiplexer_5_out), .sel(C8));
  or or_3 (or_3_out, C7, C8);
  Clock CLOCK (.out(CLK));
  Register #(.width(32)) u_RI (.D(BUS_INTERNO), .en(C6), .Q(RI), .clk(CLK), .clr(RESET));
  assign BUS_INTERNO = T7 ? IND_q : 32'bz;  // Controlled_Buffer controlled_buffer_8
  Register #(.width(32)) IND (.D(multiplexer_5_out), .en(or_3_out), .Q(IND_q), .clk(CLK), .clr(RESET));
  assign bit_extender_1_out = {{16{RI[15]}}, RI[15:0]};  // Bit_Extender bit_extender_1
  assign BUS_INTERNO = T8 ? bit_extender_1_out : 32'bz;  // Controlled_Buffer controlled_buffer_9
  assign BUS_INTERNO = T9 ? {4'b0000, RI[25:0], 2'b00} : 32'bz;  // Controlled_Buffer controlled_buffer_10
  CONTROL control_1 (
    .RI(RI), .EST(IND_q), .T1(T1), .T2(T2), .T3(T3), .T4(T4), .T5(T5), .SC(ENABLE_B), .T6(T6), .C1(C1),
    .T7(T7), .C2(C2), .T8(T8), .C3(C3), .T9(T9), .C4(C4), .C5(C5), .MB(MB), .C6(C6), .MA(MA), .C7(C7),
    .MEM_L(L), .C8(C8), .MEM_E(E), .C9(C9), .Sin_uso_2(M_Sel), .C10(C10), .TA(TA), .Sin_uso_3(C11),
    .ALU_func(func), .RC(RC), .RB(RB), .RA(RA), .RESET(RESET));  // open: Sin_uso, shamt

  // Other names for the same wires on the sheet: RST = RESET

  // Notes on the sheet:
  //   Inmediato
  //   Jump Address
  //   CONTROL
endmodule

module ALU (
  input  [31:0] Op__A,
  input  [31:0] Op__B,
  input  [5:0] C_OP,
  output [31:0] Estado,
  output [31:0] S
);

  wire Sel_aritlog_sel_al, Sel_Shift_sel_sh;
  wire [31:0] and_1_out, nor_1_out, or_1_out, S_R_s, SLL_s, SRA_s, xor_1_out;

  Sel_AritLog Sel_aritlog (.ALU_Func(C_OP[5:3]), .Sel_AL(Sel_aritlog_sel_al));
  assign and_1_out = Op__B & Op__A;  // AND_Gate and_1, 32 bits wide
  ALU_SUMA_RESTA S_R (.A(Op__A), .B(Op__B), .S_R(C_OP[0]), .S(S_R_s), .Carry(Estado[2]));
  Multiplexer #(.select(3), .width(32)) multiplexer_1 (
    .in0(S_R_s), .in1(S_R_s), .in2(S_R_s), .in3(S_R_s), .in4(and_1_out), .in5(or_1_out), .in6(xor_1_out),
    .in7(nor_1_out), .out(S), .sel(C_OP[2:0]), .en(Sel_aritlog_sel_al));
  assign xor_1_out = Op__B ^ Op__A;  // XOR_Gate xor_1, 32 bits wide
  assign or_1_out = Op__B | Op__A;  // OR_Gate or_1, 32 bits wide
  assign nor_1_out = ~(Op__B | Op__A);  // NOR_Gate nor_1, 32 bits wide
  ALU_Des_Izq SLL (.A(Op__A), .B(Op__B), .S(SLL_s));
  Multiplexer #(.select(3), .width(32)) multiplexer_2 (
    .in0(SLL_s), .in3(SRA_s), .out(S), .sel(C_OP[2:0]), .en(Sel_Shift_sel_sh));  // open: in1, in2, in4, in5, in6, in7
  Sel_Shift Sel_Shift (.ALU_Func(C_OP[5:3]), .Sel_Sh(Sel_Shift_sel_sh));
  ALU_Des_Der SRA (.A(Op__A), .B(Op__B), .S(SRA_s));
  nor nor_2 (Estado[0], S[0], S[1], S[2], S[3], S[4], S[5], S[6], S[7], S[8], S[9], S[10], S[11], S[12], S[13], S[14], S[15], S[16], S[17], S[18], S[19], S[20], S[21], S[22], S[23], S[24], S[25], S[26], S[27], S[28], S[29], S[30], S[31]);
  ExactlyOne xor_2 (
    .out(Estado[1]), .in0(S[0]), .in1(S[1]), .in2(S[2]), .in3(S[3]), .in4(S[4]), .in5(S[5]), .in6(S[6]),
    .in7(S[7]), .in8(S[8]), .in9(S[9]), .in10(S[10]), .in11(S[11]), .in12(S[12]), .in13(S[13]), .in14(S[14]),
    .in15(S[15]), .in16(S[16]), .in17(S[17]), .in18(S[18]), .in19(S[19]), .in20(S[20]), .in21(S[21]),
    .in22(S[22]), .in23(S[23]), .in24(S[24]), .in25(S[25]), .in26(S[26]), .in27(S[27]), .in28(S[28]),
    .in29(S[29]), .in30(S[30]), .in31(S[31]));

  assign Estado[31:3] = {29{1'b0}};

  // Other names for the same wires on the sheet: C = Estado[2]

  // Notes on the sheet:
  //   Estado: pull=down
endmodule

module ALU_SUMA_RESTA (
  input  [31:0] A,
  input  [31:0] B,
  input  S_R,
  output [31:0] S,
  output Carry
);

  wire [31:0] xor_1_out;

  assign xor_1_out = B ^ {32{S_R}};  // XOR_Gate xor_1, 32 bits wide
  Adder #(.width(32)) adder_1 (.a(A), .b(xor_1_out), .out(S), .cin(S_R), .cout(Carry));
endmodule

module ALU_Des_Izq (
  input  [31:0] A,
  input  [31:0] B,
  output [31:0] S
);

  wire [31:0] multiplexer_1_out, multiplexer_2_out, multiplexer_3_out, multiplexer_4_out;

  Multiplexer #(.width(32)) multiplexer_1 (
    .in0(A), .in1({A[30:0], 1'b0}), .out(multiplexer_1_out), .sel(B[0]));  // open: en
  Multiplexer #(.width(32)) multiplexer_2 (
    .in0(multiplexer_1_out), .in1({multiplexer_1_out[29:0], 2'b00}), .out(multiplexer_2_out), .sel(B[1]));  // open: en
  Multiplexer #(.width(32)) multiplexer_3 (
    .in0(multiplexer_2_out), .in1({multiplexer_2_out[27:0], 4'b0000}), .out(multiplexer_3_out), .sel(B[2]));  // open: en
  Multiplexer #(.width(32)) multiplexer_4 (
    .in0(multiplexer_3_out), .in1({multiplexer_3_out[23:0], {8{1'b0}}}), .out(multiplexer_4_out), .sel(B[3]));  // open: en
  Multiplexer #(.width(32)) multiplexer_5 (
    .in0(multiplexer_4_out), .in1({multiplexer_4_out[15:0], {16{1'b0}}}), .out(S), .sel(B[4]));  // open: en
endmodule

module ALU_Des_Der (
  input  [31:0] A,
  input  [31:0] B,
  output [31:0] S
);

  Multiplexer #(.select(2), .width(32)) multiplexer_1 (
    .in0({1'b0, A[31:1]}), .in1({2'b00, A[31:2]}), .in2({3'b000, A[31:3]}), .in3({4'b0000, A[31:4]}),
    .out(S), .sel(B[1:0]));  // open: en
endmodule

module CONTROL (
  input  [31:0] RI,
  input  RESET,
  input  [31:0] EST,
  output T1,
  output T2,
  output T3,
  output T4,
  output T5,
  output SC,
  output T6,
  output C1,
  output T7,
  output C2,
  output T8,
  output C3,
  output T9,
  output C4,
  output Sin_uso,
  output C5,
  output MB,
  output C6,
  output MA,
  output C7,
  output MEM_L,
  output C8,
  output MEM_E,
  output C9,
  output Sin_uso_2,
  output C10,
  output TA,
  output Sin_uso_3,
  output [5:0] ALU_func,
  output [4:0] shamt,
  output [4:0] RC,
  output [4:0] RB,
  output [4:0] RA
);

  wire clock_1_out, EXEC, NEXT, Type_I;
  wire [3:3] rom_2_data;
  wire [7:0] adder_1_out, multiplexer_1_out, rom_1_data, RuI_q;

  ROM #(.addrWidth(6)) rom_1 (.addr(RI[31:26]), .data(rom_1_data));  // open: sel
  Adder adder_1 (.a(RuI_q), .b(8'h1), .out(adder_1_out));  // open: cin, cout
  Multiplexer #(.select(2), .width(8), .disabled(0), .enable("false")) multiplexer_1 (
    .in0({8{1'b0}}), .in1(adder_1_out), .in2(rom_1_data), .out(multiplexer_1_out), .sel({EXEC, NEXT}));  // open: in3
  Register RuI (.D(multiplexer_1_out), .Q(RuI_q), .clk(clock_1_out), .clr(RESET));  // open: en
  Clock clock_1 (.out(clock_1_out));
  ROM #(.dataWidth(32)) rom_2 (
    .addr(RuI_q),
    .data({TA, Sin_uso_2, MEM_E, MEM_L, MA, MB, Sin_uso, T9, T8, T7, T6, T5, T4, T3, T2, T1, Sin_uso_3, C10, C9, C8, C7, C6, C5, C4, C3, C2, C1, SC, rom_2_data[3], Type_I, EXEC, NEXT}));  // open: sel

  assign ALU_func = RI[5:0];
  assign RA = RI[25:21];
  assign RB = RI[20:16];
  assign RC = RI[15:11];
  assign shamt = RI[10:6];

  // Notes on the sheet:
  //   Sin_uso_2: pull=down
  //   C7: pull=down
  //   T1: pull=down
  //   TA: pull=down
  //   Sin_uso: pull=down
  //   C6: pull=down
  //   T4: pull=down
  //   T3: pull=down
  //   MA: pull=down
  //   C4: pull=down
  //   T2: pull=down
  //   T7: pull=down
  //   C3: pull=down
  //   Sin_uso_3: pull=down
  //   C2: pull=down
  //   C9: pull=down
  //   MB: pull=down
  //   RESET: pull=down
  //   C10: pull=down
  //   SC: pull=down
  //   MEM_E: pull=down
  //   C8: pull=down
  //   C5: pull=down
  //   C1: pull=down
  //   T8: pull=down
  //   T6: pull=down
  //   RI: pull=down
  //   T9: pull=down
  //   MEM_L: pull=down
  //   T5: pull=down
  //   OPCODE
  //   Tabla direcciones
  //   Bits 19-16: Triestados
  //   Bits 23-20: Triestados
  //   Bits 27-24: Triestados y MUX
  //   Bits 31-28: Control Memoria
  //   contents of rom_1 (hex, n*v repeats v):
  //   5 7*0 5
  //   Bits 7-4: Señales captura
  //   Bits15-12: Señales de captura
  //   Bits 3-0: MUX A y B; Control interno de la UC
  //   Bits 11-8: Señales captura
  //   Memoria de Microinstrucciones
  //   contents of rom_2 (hex, n*v repeats v):
  //   80021 30000141 2040401 2 0 1000010 802006 8100015
  //   NEXT: Pasar a siguiente microinstrucción en el siguiente ciclo
  //   EXEC: RI está cargado; pasar a fase ejecución
  //   Type_I: La instrucción en ejecución es de tipo I (con dato inmediato)
  //   [NEXT,EXEC] = control de flujo de la UC:
  //   00: Reset (vuelve a FETCH)
  //   10 = Exec: salta a la uInstr indicada por la tabla de direcciones
  //   11: No usado
  //   01 = Next: pasa a siguiente u-Instr en el siguiente ciclo
endmodule

module Generador_uInstr (
  input  T1,
  input  Next,
  input  T2,
  input  EXEC,
  input  T3,
  input  Type_I,
  input  T4,
  input  T5,
  input  SC,
  input  T6,
  input  C1,
  input  T7,
  input  C2,
  input  T8,
  input  C3,
  input  T9,
  input  C4,
  input  Sin_uso,
  input  C5,
  input  MB,
  input  C6,
  input  MA,
  input  C7,
  input  MEM_L,
  input  C8,
  input  MEM_E,
  input  C9,
  input  Sin_uso_2,
  input  C10,
  input  TA,
  input  Sin_uso_3
);

  Hex_Digit_Display hex_digit_display_1 (.value({TA, Sin_uso_2, MEM_E, MEM_L}));  // open: dp
  Hex_Digit_Display hex_digit_display_2 (.value({T8, T7, T6, T5}));  // open: dp
  Hex_Digit_Display hex_digit_display_3 (.value({MA, MB, Sin_uso, T9}));  // open: dp
  Hex_Digit_Display hex_digit_display_4 (.value({T4, T3, T2, T1}));  // open: dp
  Hex_Digit_Display hex_digit_display_5 (.value({Sin_uso_3, C10, C9, C8}));  // open: dp
  Hex_Digit_Display hex_digit_display_6 (.value({C3, C2, C1, SC}));  // open: dp
  Hex_Digit_Display hex_digit_display_7 (.value({C7, C6, C5, C4}));  // open: dp
  Hex_Digit_Display hex_digit_display_8 (.value({1'b0, Type_I, EXEC, Next}));  // open: dp

  // Notes on the sheet:
  //   MEM_L: pull=down
  //   T1: pull=down
  //   T8: pull=down
  //   C6: pull=down
  //   MEM_E: pull=down
  //   T6: pull=down
  //   C2: pull=down
  //   C7: pull=down
  //   C1: pull=down
  //   C9: pull=down
  //   SC: pull=down
  //   Next: pull=down
  //   C5: pull=down
  //   C3: pull=down
  //   MB: pull=down
  //   T3: pull=down
  //   T9: pull=down
  //   T7: pull=down
  //   Sin_uso: pull=down
  //   T5: pull=down
  //   Sin_uso_2: pull=down
  //   C4: pull=down
  //   TA: pull=down
  //   MA: pull=down
  //   EXEC: pull=down
  //   Sin_uso_3: pull=down
  //   C10: pull=down
  //   T2: pull=down
  //   C8: pull=down
  //   T4: pull=down
  //   Type_I: pull=down
  //   Bits 19-16: Triestados
  //   Bits 23-20: Triestados
  //   Bits 27-24: Triestados y MUX
  //   Bits 31-28: Control Memoria
  //   Bits 3-0: MUX A y B; Control interno de la UC
  //   Bits 7-4: Señales captura
  //   Bits 11-8: Señales captura
  //   Bits15-12: Señales de captura
endmodule

module Sel_AritLog (
  input  [2:0] ALU_Func,
  output Sel_AL
);

  wire and_1_out, and_2_out;

  and and_1 (and_1_out, ~ALU_Func[0], ~ALU_Func[1], ALU_Func[2]);  // AND_Gate
  and and_2 (and_2_out, ALU_Func[0], ~ALU_Func[1], ~ALU_Func[2]);  // AND_Gate
  or or_1 (Sel_AL, and_1_out, and_2_out);

  // Notes on the sheet:
  //   ALU_func == 001: Suma, resta u op. lógica tipo I
  //   ALU_func == 100: Suma, resta u op. lógica tipo R
endmodule

module Sel_Shift (
  input  [2:0] ALU_Func,
  output Sel_Sh
);

  and and_1 (Sel_Sh, ~ALU_Func[0], ~ALU_Func[1], ~ALU_Func[2]);  // AND_Gate

  // Notes on the sheet:
  //   ALU_func == 000: Desplazamiento de bits
endmodule
