// Logisim project CPU_MIPS_v3.9.circ as structural Verilog: 8 circuits, main circuit Main
module BANCO (
  input  [4:0] RA,
  input  [4:0] RB,
  input  [4:0] RC,
  input  [31:0] C_IN,
  input  Load_EN,
  input  CLOCK_IN,
  input  RESET_IN,
  output [31:0] A_OUT,
  output [31:0] B_OUT
);

  wire [3:0] demultiplexer_2_out0, demultiplexer_2_out4, demultiplexer_2_out8, demultiplexer_2_out12,
       demultiplexer_2_out16, demultiplexer_2_out20, demultiplexer_2_out24, demultiplexer_2_out31;
  wire [31:0] a0_q, at_q, demultiplexer_1_out0, demultiplexer_1_out1, demultiplexer_1_out2,
       demultiplexer_1_out3, demultiplexer_1_out4, demultiplexer_1_out5, demultiplexer_1_out6,
       demultiplexer_1_out7, demultiplexer_1_out8, demultiplexer_1_out9, demultiplexer_1_out10,
       demultiplexer_1_out11, demultiplexer_1_out12, demultiplexer_1_out13, demultiplexer_1_out14,
       demultiplexer_1_out15, demultiplexer_1_out16, demultiplexer_1_out17, demultiplexer_1_out18,
       demultiplexer_1_out19, demultiplexer_1_out20, demultiplexer_1_out21, demultiplexer_1_out22,
       demultiplexer_1_out23, demultiplexer_1_out24, demultiplexer_1_out25, demultiplexer_1_out26,
       demultiplexer_1_out27, demultiplexer_1_out28, demultiplexer_1_out29, demultiplexer_1_out30,
       demultiplexer_1_out31, ra_q, register_1_q, register_2_q, register_3_q, register_4_q, register_5_q,
       register_6_q, register_7_q, register_8_q, register_9_q, register_10_q, register_11_q, register_12_q,
       register_13_q, register_14_q, register_15_q, register_16_q, register_17_q, register_18_q,
       register_19_q, register_20_q, register_21_q, s0_q, s4_q, t0_q, t4_q, t8_q, v0_q, v1_q, zero_q;

  Register #(.width(32)) zero (.D(demultiplexer_1_out0), .en(1'b0), .Q(zero_q), .clk(CLOCK_IN), .clr(RESET_IN));
  Register #(.width(32)) at (
    .D(demultiplexer_1_out1), .en(demultiplexer_2_out0[1]), .Q(at_q), .clk(CLOCK_IN), .clr(RESET_IN));
  Register #(.width(32)) v0 (
    .D(demultiplexer_1_out2), .en(demultiplexer_2_out0[2]), .Q(v0_q), .clk(CLOCK_IN), .clr(RESET_IN));
  Register #(.width(32)) v1 (
    .D(demultiplexer_1_out3), .en(demultiplexer_2_out0[3]), .Q(v1_q), .clk(CLOCK_IN), .clr(RESET_IN));
  Demultiplexer #(.select(5), .width(32)) demultiplexer_1 (
    .out0(demultiplexer_1_out0), .out1(demultiplexer_1_out1), .out2(demultiplexer_1_out2),
    .out3(demultiplexer_1_out3), .out4(demultiplexer_1_out4), .out5(demultiplexer_1_out5),
    .out6(demultiplexer_1_out6), .out7(demultiplexer_1_out7), .out8(demultiplexer_1_out8),
    .out9(demultiplexer_1_out9), .out10(demultiplexer_1_out10), .out11(demultiplexer_1_out11),
    .out12(demultiplexer_1_out12), .out13(demultiplexer_1_out13), .out14(demultiplexer_1_out14),
    .out15(demultiplexer_1_out15), .out16(demultiplexer_1_out16), .out17(demultiplexer_1_out17),
    .out18(demultiplexer_1_out18), .out19(demultiplexer_1_out19), .out20(demultiplexer_1_out20),
    .out21(demultiplexer_1_out21), .out22(demultiplexer_1_out22), .out23(demultiplexer_1_out23),
    .out24(demultiplexer_1_out24), .out25(demultiplexer_1_out25), .out26(demultiplexer_1_out26),
    .out27(demultiplexer_1_out27), .out28(demultiplexer_1_out28), .out29(demultiplexer_1_out29),
    .out30(demultiplexer_1_out30), .out31(demultiplexer_1_out31), .in(C_IN), .sel(RC));  // open: en
  Register #(.width(32)) a0 (
    .D(demultiplexer_1_out4), .en(demultiplexer_2_out4[0]), .Q(a0_q), .clk(CLOCK_IN), .clr(RESET_IN));
  Register #(.width(32)) register_1 (
    .D(demultiplexer_1_out5), .en(demultiplexer_2_out4[1]), .Q(register_1_q), .clk(CLOCK_IN), .clr(RESET_IN));
  Register #(.width(32)) register_2 (
    .D(demultiplexer_1_out6), .en(demultiplexer_2_out4[2]), .Q(register_2_q), .clk(CLOCK_IN), .clr(RESET_IN));
  Register #(.width(32)) register_3 (
    .D(demultiplexer_1_out7), .en(demultiplexer_2_out4[3]), .Q(register_3_q), .clk(CLOCK_IN), .clr(RESET_IN));
  Register #(.width(32)) t0 (
    .D(demultiplexer_1_out8), .en(demultiplexer_2_out8[0]), .Q(t0_q), .clk(CLOCK_IN), .clr(RESET_IN));
  Register #(.width(32)) register_4 (
    .D(demultiplexer_1_out9), .en(demultiplexer_2_out8[1]), .Q(register_4_q), .clk(CLOCK_IN), .clr(RESET_IN));
  Register #(.width(32)) register_5 (
    .D(demultiplexer_1_out10), .en(demultiplexer_2_out8[2]), .Q(register_5_q), .clk(CLOCK_IN), .clr(RESET_IN));
  Register #(.width(32)) register_6 (
    .D(demultiplexer_1_out11), .en(demultiplexer_2_out8[3]), .Q(register_6_q), .clk(CLOCK_IN), .clr(RESET_IN));
  Register #(.width(32)) t4 (
    .D(demultiplexer_1_out12), .en(demultiplexer_2_out12[0]), .Q(t4_q), .clk(CLOCK_IN), .clr(RESET_IN));
  Register #(.width(32)) register_7 (
    .D(demultiplexer_1_out13), .en(demultiplexer_2_out12[1]), .Q(register_7_q), .clk(CLOCK_IN), .clr(RESET_IN));
  Register #(.width(32)) register_8 (
    .D(demultiplexer_1_out14), .en(demultiplexer_2_out12[2]), .Q(register_8_q), .clk(CLOCK_IN), .clr(RESET_IN));
  Register #(.width(32)) register_9 (
    .D(demultiplexer_1_out15), .en(demultiplexer_2_out12[3]), .Q(register_9_q), .clk(CLOCK_IN), .clr(RESET_IN));
  Register #(.width(32)) s0 (
    .D(demultiplexer_1_out16), .en(demultiplexer_2_out16[0]), .Q(s0_q), .clk(CLOCK_IN), .clr(RESET_IN));
  Register #(.width(32)) register_10 (
    .D(demultiplexer_1_out17), .en(demultiplexer_2_out16[1]), .Q(register_10_q), .clk(CLOCK_IN),
    .clr(RESET_IN));
  Register #(.width(32)) register_11 (
    .D(demultiplexer_1_out18), .en(demultiplexer_2_out16[2]), .Q(register_11_q), .clk(CLOCK_IN),
    .clr(RESET_IN));
  Register #(.width(32)) register_12 (
    .D(demultiplexer_1_out19), .en(demultiplexer_2_out16[3]), .Q(register_12_q), .clk(CLOCK_IN),
    .clr(RESET_IN));
  Register #(.width(32)) s4 (
    .D(demultiplexer_1_out20), .en(demultiplexer_2_out20[0]), .Q(s4_q), .clk(CLOCK_IN), .clr(RESET_IN));
  Register #(.width(32)) register_13 (
    .D(demultiplexer_1_out21), .en(demultiplexer_2_out20[1]), .Q(register_13_q), .clk(CLOCK_IN),
    .clr(RESET_IN));
  Register #(.width(32)) register_14 (
    .D(demultiplexer_1_out22), .en(demultiplexer_2_out20[2]), .Q(register_14_q), .clk(CLOCK_IN),
    .clr(RESET_IN));
  Register #(.width(32)) register_15 (
    .D(demultiplexer_1_out23), .en(demultiplexer_2_out20[3]), .Q(register_15_q), .clk(CLOCK_IN),
    .clr(RESET_IN));
  Register #(.width(32)) t8 (
    .D(demultiplexer_1_out24), .en(demultiplexer_2_out24[0]), .Q(t8_q), .clk(CLOCK_IN), .clr(RESET_IN));
  Register #(.width(32)) register_16 (
    .D(demultiplexer_1_out25), .en(demultiplexer_2_out24[1]), .Q(register_16_q), .clk(CLOCK_IN),
    .clr(RESET_IN));
  Register #(.width(32)) register_17 (
    .D(demultiplexer_1_out26), .en(demultiplexer_2_out24[2]), .Q(register_17_q), .clk(CLOCK_IN),
    .clr(RESET_IN));
  Register #(.width(32)) register_18 (
    .D(demultiplexer_1_out27), .en(demultiplexer_2_out24[3]), .Q(register_18_q), .clk(CLOCK_IN),
    .clr(RESET_IN));
  Register #(.width(32)) register_19 (
    .D(demultiplexer_1_out28), .en(demultiplexer_2_out31[0]), .Q(register_19_q), .clk(CLOCK_IN),
    .clr(RESET_IN));
  Register #(.width(32)) register_20 (
    .D(demultiplexer_1_out29), .en(demultiplexer_2_out31[1]), .Q(register_20_q), .clk(CLOCK_IN),
    .clr(RESET_IN));
  Register #(.width(32)) register_21 (
    .D(demultiplexer_1_out30), .en(demultiplexer_2_out31[2]), .Q(register_21_q), .clk(CLOCK_IN),
    .clr(RESET_IN));
  Register #(.width(32)) u_ra (
    .D(demultiplexer_1_out31), .en(demultiplexer_2_out31[3]), .Q(ra_q), .clk(CLOCK_IN), .clr(RESET_IN));
  Demultiplexer #(.select(5), .enable("false")) demultiplexer_2 (
    .out0(demultiplexer_2_out0[0]), .out1(demultiplexer_2_out0[1]), .out2(demultiplexer_2_out0[2]),
    .out3(demultiplexer_2_out0[3]), .out4(demultiplexer_2_out4[0]), .out5(demultiplexer_2_out4[1]),
    .out6(demultiplexer_2_out4[2]), .out7(demultiplexer_2_out4[3]), .out8(demultiplexer_2_out8[0]),
    .out9(demultiplexer_2_out8[1]), .out10(demultiplexer_2_out8[2]), .out11(demultiplexer_2_out8[3]),
    .out12(demultiplexer_2_out12[0]), .out13(demultiplexer_2_out12[1]), .out14(demultiplexer_2_out12[2]),
    .out15(demultiplexer_2_out12[3]), .out16(demultiplexer_2_out16[0]), .out17(demultiplexer_2_out16[1]),
    .out18(demultiplexer_2_out16[2]), .out19(demultiplexer_2_out16[3]), .out20(demultiplexer_2_out20[0]),
    .out21(demultiplexer_2_out20[1]), .out22(demultiplexer_2_out20[2]), .out23(demultiplexer_2_out20[3]),
    .out24(demultiplexer_2_out24[0]), .out25(demultiplexer_2_out24[1]), .out26(demultiplexer_2_out24[2]),
    .out27(demultiplexer_2_out24[3]), .out28(demultiplexer_2_out31[3]), .out29(demultiplexer_2_out31[1]),
    .out30(demultiplexer_2_out31[2]), .out31(demultiplexer_2_out31[0]), .in(Load_EN), .sel(RC));
  Multiplexer #(.select(5), .width(32), .enable("false")) multiplexer_1 (
    .in0(zero_q), .in1(at_q), .in2(v0_q), .in3(v1_q), .in4(a0_q), .in5(register_1_q), .in6(register_2_q),
    .in7(register_3_q), .in8(t0_q), .in9(register_4_q), .in10(register_5_q), .in11(register_6_q),
    .in12(t4_q), .in13(register_7_q), .in14(register_8_q), .in15(register_9_q), .in16(s0_q),
    .in17(register_10_q), .in18(register_11_q), .in19(register_12_q), .in20(s4_q), .in21(register_13_q),
    .in22(register_14_q), .in23(register_15_q), .in24(t8_q), .in25(register_16_q), .in26(register_17_q),
    .in27(register_18_q), .in28(register_19_q), .in29(register_20_q), .in30(register_21_q), .in31(ra_q),
    .out(A_OUT), .sel(RA));
  Multiplexer #(.select(5), .width(32), .disabled(0), .enable("false")) multiplexer_2 (
    .in0(zero_q), .in1(at_q), .in2(v0_q), .in3(v1_q), .in4(a0_q), .in5(register_1_q), .in6(register_2_q),
    .in7(register_3_q), .in8(t0_q), .in9(register_4_q), .in10(register_5_q), .in11(register_6_q),
    .in12(t4_q), .in13(register_7_q), .in14(register_8_q), .in15(register_9_q), .in16(s0_q),
    .in17(register_10_q), .in18(register_11_q), .in19(register_12_q), .in20(s4_q), .in21(register_13_q),
    .in22(register_14_q), .in23(register_15_q), .in24(t8_q), .in25(register_16_q), .in26(register_17_q),
    .in27(register_18_q), .in28(register_19_q), .in29(register_20_q), .in30(register_21_q), .in31(ra_q),
    .out(B_OUT), .sel(RB));

  // Other names for the same wires on the sheet: CLK = CLOCK_IN; RST = RESET_IN
endmodule

// MAIN
module Main (
  input  Sel,
  input  L,
  input  TA,
  input  C6,
  input  C2,
  input  C4,
  input  C3,
  input  C5,
  input  C1,
  input  T3,
  input  T4,
  input  T8,
  input  T9,
  input  T7,
  input  T1,
  input  T2,
  input  T5,
  input  T6,
  input  C9,
  input  C10,
  input  C7,
  input  C8,
  input  MA,
  input  MB,
  input  [4:0] RA,
  input  [5:0] ALU_func,
  input  [4:0] RB,
  input  [4:0] RC,
  input  RESET,
  input  CB,
  input  C11,
  output [31:0] BUS_DE_DATOS,
  output [31:0] BUS_INTERNO,
  output [31:0] INDICADORES,
  output [31:0] SALIDA_ALU
);

  wire CLK, or_1_out, or_2_out, or_3_out;
  wire [1:0] MAR_q_2;
  wire [27:2] RI_q_2;
  wire [31:0] adder_1_out, banco_1_a_out, banco_1_b_out, bit_extender_1_out, IND_q, MAR_q, MBR_q,
       multiplexer_1_out, multiplexer_2_out, multiplexer_3_out, multiplexer_4_out, multiplexer_5_out, PC_q,
       RT1_q, RT2_q, RT3_q;
  wire [31:26] RI_q;

  Register #(.width(32), .trigger("falling")) MAR (
    .D(BUS_INTERNO), .en(C1), .Q({MAR_q[31:14], MAR_q_2, MAR_q[11:0]}), .clk(CLK), .clr(RESET));
  assign BUS_INTERNO = T1 ? banco_1_a_out : 32'bz;  // Controlled_Buffer controlled_buffer_1
  assign BUS_INTERNO = T2 ? banco_1_b_out : 32'bz;  // Controlled_Buffer controlled_buffer_2
  BANCO banco_1 (
    .RA(RA), .RB(RB), .RC(RC), .C_IN(BUS_INTERNO), .Load_EN(CB), .CLOCK_IN(CLK), .RESET_IN(RESET),
    .A_OUT(banco_1_a_out), .B_OUT(banco_1_b_out));
  Register #(.width(32), .trigger("falling")) RT1 (.D(BUS_INTERNO), .en(C9), .Q(RT1_q), .clk(CLK), .clr(RESET));
  Multiplexer #(.width(32), .enable("false")) multiplexer_1 (
    .in0(banco_1_a_out), .in1(RT1_q), .out(multiplexer_1_out), .sel(MA));
  ALU alu_1 (
    .Op__A(multiplexer_1_out), .Op__B(multiplexer_3_out), .C_OP(ALU_func), .Estado(INDICADORES),
    .S(SALIDA_ALU));
  RAM #(.addrWidth(24), .dataWidth(32)) ram_1 (
    .addr({MAR_q[25:14], MAR_q_2, MAR_q[11:2]}), .data(BUS_DE_DATOS), .sel(Sel), .clk(CLK), .ld(L));  // open: clr
  Multiplexer #(.width(32), .enable("false")) multiplexer_2 (
    .in0(BUS_DE_DATOS), .in1(BUS_INTERNO), .out(multiplexer_2_out), .sel(C3));
  or or_1 (or_1_out, C2, C3);
  assign BUS_DE_DATOS = TA ? MBR_q : 32'bz;  // Controlled_Buffer controlled_buffer_3
  Register #(.width(32), .trigger("falling")) MBR (
    .D(multiplexer_2_out), .en(or_1_out), .Q(MBR_q), .clk(CLK), .clr(RESET));
  assign BUS_INTERNO = T3 ? MBR_q : 32'bz;  // Controlled_Buffer controlled_buffer_4
  assign BUS_INTERNO = T5 ? SALIDA_ALU : 32'bz;  // Controlled_Buffer controlled_buffer_5
  Register #(.width(32), .trigger("falling")) RT2 (.D(BUS_INTERNO), .en(C10), .Q(RT2_q), .clk(CLK), .clr(RESET));
  Multiplexer #(.width(32), .enable("false")) multiplexer_3 (
    .in0(banco_1_b_out), .in1(RT2_q), .out(multiplexer_3_out), .sel(MB));
  assign BUS_INTERNO = T6 ? RT3_q : 32'bz;  // Controlled_Buffer controlled_buffer_6
  Register #(.width(32), .trigger("falling")) RT3 (.D(SALIDA_ALU), .en(C11), .Q(RT3_q), .clk(CLK), .clr(RESET));
  Adder #(.width(32)) adder_1 (.a(PC_q), .b(32'h4), .out(adder_1_out));  // open: cin, cout
  Register #(.width(32), .trigger("falling")) PC (
    .D(multiplexer_4_out), .en(or_2_out), .Q(PC_q), .clk(CLK), .clr(RESET));
  Multiplexer #(.width(32), .enable("false")) multiplexer_4 (
    .in0(adder_1_out), .in1(BUS_INTERNO), .out(multiplexer_4_out), .sel(C5));
  or or_2 (or_2_out, C4, C5);
  Clock CLOCK (.out(CLK));
  assign BUS_INTERNO = T4 ? PC_q : 32'bz;  // Controlled_Buffer controlled_buffer_7
  Multiplexer #(.width(32), .enable("false")) multiplexer_5 (
    .in0(BUS_INTERNO), .in1(INDICADORES), .out(multiplexer_5_out), .sel(C8));
  or or_3 (or_3_out, C7, C8);
  Register #(.width(32), .trigger("falling")) RI (.D(BUS_INTERNO), .en(C6), .Q({RI_q, RI_q_2}), .clk(CLK), .clr(RESET));
  assign BUS_INTERNO = T7 ? IND_q : 32'bz;  // Controlled_Buffer controlled_buffer_8
  Register #(.width(32), .trigger("falling")) IND (
    .D(multiplexer_5_out), .en(or_3_out), .Q(IND_q), .clk(CLK), .clr(RESET));
  assign bit_extender_1_out = {{16{RI_q_2[17]}}, RI_q_2[17:2]};  // Bit_Extender bit_extender_1
  assign BUS_INTERNO = T8 ? bit_extender_1_out : 32'bz;  // Controlled_Buffer controlled_buffer_9
  assign BUS_INTERNO = T9 ? {4'b0000, RI_q_2, 2'b00} : 32'bz;  // Controlled_Buffer controlled_buffer_10

  // Other names for the same wires on the sheet: RST = RESET

  // Notes on the sheet:
  //   Uso de la memoria:
  //   Sel: activa el módulo de memoria (solo para lectura o solo para escritura, según el valor de L)
  //   L: Lectura/escritura. Con L=1 y Sel=1 se activa la salida de la memoria (modo lectura)
  //   CLK: Las escrituras (con Sel=1 y L=0) se producen en el flanco de subida del reloj.
  //   Con L=0 y Sel=1 se activa la escritura en la memoria
  //   Inmediato
  //   CTRL+T: conmutar el reloj
  //   Jump Address
endmodule

module ALU (
  input  [31:0] Op__A,
  input  [31:0] Op__B,
  input  [5:0] C_OP,
  output [31:0] Estado,
  output [31:0] S
);

  wire Sel_aritlog_sel_al, Sel_Shift_sel_sh;
  wire [31:0] and_1_out, nor_1_out, or_1_out, S_R_s, SLL_s, SRA_s, xor_1_out;

  Sel_AritLog Sel_aritlog (.ALU_Func(C_OP[5:3]), .Sel_AL(Sel_aritlog_sel_al));
  assign and_1_out = Op__B & Op__A;  // AND_Gate and_1, 32 bits wide
  ALU_SUMA_RESTA S_R (.A(Op__A), .B(Op__B), .S_R(C_OP[0]), .S(S_R_s), .Carry(Estado[2]));
  Multiplexer #(.select(3), .width(32)) multiplexer_1 (
    .in0(S_R_s), .in1(S_R_s), .in2(S_R_s), .in3(S_R_s), .in4(and_1_out), .in5(or_1_out), .in6(xor_1_out),
    .in7(nor_1_out), .out({Estado[3], S[30:0]}), .sel(C_OP[2:0]), .en(Sel_aritlog_sel_al));
  assign xor_1_out = Op__B ^ Op__A;  // XOR_Gate xor_1, 32 bits wide
  assign or_1_out = Op__B | Op__A;  // OR_Gate or_1, 32 bits wide
  assign nor_1_out = ~(Op__B | Op__A);  // NOR_Gate nor_1, 32 bits wide
  ALU_Des_Izq SLL (.A(Op__A), .B(Op__B), .S(SLL_s));
  Multiplexer #(.select(3), .width(32)) multiplexer_2 (
    .in0(SLL_s), .in3(SRA_s), .out({Estado[3], S[30:0]}), .sel(C_OP[2:0]), .en(Sel_Shift_sel_sh));  // open: in1, in2, in4, in5, in6, in7
  Sel_Shift Sel_Shift (.ALU_Func(C_OP[5:3]), .Sel_Sh(Sel_Shift_sel_sh));
  ALU_Des_Der SRA (.A(Op__A), .B(Op__B), .S(SRA_s));
  nor nor_2 (Estado[0], S[0], S[1], S[2], S[3], S[4], S[5], S[6], S[7], S[8], S[9], S[10], S[11], S[12], S[13], S[14], S[15], S[16], S[17], S[18], S[19], S[20], S[21], S[22], S[23], S[24], S[25], S[26], S[27], S[28], S[29], S[30], Estado[3]);
  ExactlyOne xor_2 (
    .out(Estado[1]), .in0(S[0]), .in1(S[1]), .in2(S[2]), .in3(S[3]), .in4(S[4]), .in5(S[5]), .in6(S[6]),
    .in7(S[7]), .in8(S[8]), .in9(S[9]), .in10(S[10]), .in11(S[11]), .in12(S[12]), .in13(S[13]), .in14(S[14]),
    .in15(S[15]), .in16(S[16]), .in17(S[17]), .in18(S[18]), .in19(S[19]), .in20(S[20]), .in21(S[21]),
    .in22(S[22]), .in23(S[23]), .in24(S[24]), .in25(S[25]), .in26(S[26]), .in27(S[27]), .in28(S[28]),
    .in29(S[29]), .in30(S[30]), .in31(Estado[3]));

  assign Estado[31:4] = {28{1'b0}};
  assign S[31] = Estado[3];

  // Other names for the same wires on the sheet: C = Estado[2]

  // Notes on the sheet:
  //   Estado: pull=down
endmodule

module ALU_SUMA_RESTA (
  input  [31:0] A,
  input  [31:0] B,
  input  S_R,
  output [31:0] S,
  output Carry
);

  wire [31:0] xor_1_out;

  assign xor_1_out = B ^ {32{S_R}};  // XOR_Gate xor_1, 32 bits wide
  Adder #(.width(32)) adder_1 (.a(A), .b(xor_1_out), .out(S), .cin(S_R), .cout(Carry));
endmodule

module ALU_Des_Izq (
  input  [31:0] A,
  input  [31:0] B,
  output [31:0] S
);

  wire [31:0] multiplexer_1_out, multiplexer_2_out, multiplexer_3_out, multiplexer_4_out;

  Multiplexer #(.width(32)) multiplexer_1 (
    .in0(A), .in1({A[30:0], 1'b0}), .out(multiplexer_1_out), .sel(B[0]));  // open: en
  Multiplexer #(.width(32)) multiplexer_2 (
    .in0(multiplexer_1_out), .in1({multiplexer_1_out[29:0], 2'b00}), .out(multiplexer_2_out), .sel(B[1]));  // open: en
  Multiplexer #(.width(32)) multiplexer_3 (
    .in0(multiplexer_2_out), .in1({multiplexer_2_out[27:0], 4'b0000}), .out(multiplexer_3_out), .sel(B[2]));  // open: en
  Multiplexer #(.width(32)) multiplexer_4 (
    .in0(multiplexer_3_out), .in1({multiplexer_3_out[23:0], {8{1'b0}}}), .out(multiplexer_4_out), .sel(B[3]));  // open: en
  Multiplexer #(.width(32)) multiplexer_5 (
    .in0(multiplexer_4_out), .in1({multiplexer_4_out[15:0], {16{1'b0}}}), .out(S), .sel(B[4]));  // open: en
endmodule

module ALU_Des_Der (
  input  [31:0] A,
  input  [31:0] B,
  output [31:0] S
);

  Multiplexer #(.select(2), .width(32)) multiplexer_1 (
    .in0({1'b0, A[31:1]}), .in1({2'b00, A[31:2]}), .in2({3'b000, A[31:3]}), .in3({4'b0000, A[31:4]}),
    .out(S), .sel(B[1:0]));  // open: en
endmodule

module Sel_AritLog (
  input  [2:0] ALU_Func,
  output Sel_AL
);

  wire and_1_out, and_2_out;

  and and_1 (and_1_out, ~ALU_Func[0], ~ALU_Func[1], ALU_Func[2]);  // AND_Gate
  and and_2 (and_2_out, ALU_Func[0], ~ALU_Func[1], ~ALU_Func[2]);  // AND_Gate
  or or_1 (Sel_AL, and_1_out, and_2_out);

  // Notes on the sheet:
  //   ALU_func == 001: Suma, resta u op. lógica tipo I
  //   ALU_func == 100: Suma, resta u op. lógica tipo R
endmodule

module Sel_Shift (
  input  [2:0] ALU_Func,
  output Sel_Sh
);

  and and_1 (Sel_Sh, ~ALU_Func[0], ~ALU_Func[1], ~ALU_Func[2]);  // AND_Gate

  // Notes on the sheet:
  //   ALU_func == 000: Desplazamiento de bits
endmodule
