// Logisim project Practica 5.2.circ as structural Verilog: 1 circuit, main circuit main
module main (
  input  [7:0] in_1,
  input  in_2,
  input  [22:0] in_3,
  input  in_4,
  output [7:0] out_5
);

  wire decoder_1_out0, decoder_1_out1, decoder_1_out2, decoder_1_out3;

  Decoder #(.select(2)) decoder_1 (
    .out0(decoder_1_out0), .out1(decoder_1_out1), .out2(decoder_1_out2), .out3(decoder_1_out3),
    .sel(in_3[22:21]));  // open: en
  assign out_5 = in_2 ? in_1 : 8'bz;  // Controlled_Buffer controlled_buffer_1
  RAM #(.addrWidth(21), .dataWidth(4)) ram_1 (
    .addr(in_3[20:0]), .data(out_5[3:0]), .sel(decoder_1_out0), .ld(in_4));  // open: clk, clr
  RAM #(.addrWidth(21), .dataWidth(4)) ram_2 (
    .addr(in_3[20:0]), .data(out_5[3:0]), .sel(decoder_1_out1), .ld(in_4));  // open: clk, clr
  RAM #(.addrWidth(21), .dataWidth(4)) ram_3 (
    .addr(in_3[20:0]), .data(out_5[3:0]), .sel(decoder_1_out2), .ld(in_4));  // open: clk, clr
  RAM #(.addrWidth(21), .dataWidth(4)) ram_4 (
    .addr(in_3[20:0]), .data(out_5[7:4]), .sel(decoder_1_out0), .ld(in_4));  // open: clk, clr
  RAM #(.addrWidth(21), .dataWidth(4)) ram_5 (
    .addr(in_3[20:0]), .data(out_5[7:4]), .sel(decoder_1_out1), .ld(in_4));  // open: clk, clr
  RAM #(.addrWidth(21), .dataWidth(4)) ram_6 (
    .addr(in_3[20:0]), .data(out_5[7:4]), .sel(decoder_1_out2), .ld(in_4));  // open: clk, clr
  // also tied to GND on the sheet: decoder_1_out3
endmodule
